# Fritzing sketch Initial_Diagram (saved by Fritzing 0.9.3b)
breadboards: 1

parts:
  WATER_PUMP1 = water pump/motor  # not connected
  Capacitive_Soil_Moisture_Sensor1 = DFRobot Capacitive Soil Moisture Sensor V1.0 [part_number=SEN0193]
  D1 = Diode [package=diode-1n4001]
  Q1 = NPN-Transistor [package="TO92 [THT]"]
  Water_Level_Sensor1 = Water Level Sensor
  Mod1 = KY-019 5V Relay Module [package="Breakout board"]
  U1 = atmega328 [package=dip]
  XTAL1 = Crystal [frequency="16 Mhz" package=THT]
  C1 = Capacitor [package=cap-pth-small2]
  C2 = Capacitor [package=cap-pth-small2]
  C4 = Electrolytic Capacitor [capacitance=1µF package="0405 [SMD, electrolytic]"]
  R1 = Resistor [tolerance=±5% resistance=10k package="0402 [SMD]"]
  VCC1 = Battery block 9V
  S1 = Round Pushbutton
  U2 = ESP8266 WiFi Module [part_number=ESP8266]
  R2 = Resistor [tolerance=±5% resistance=10k package="0402 [SMD]"]

nets:
  N1: Capacitive_Soil_Moisture_Sensor1.A, U1.D9_(PWM)
  VCC: Capacitive_Soil_Moisture_Sensor1.VCC, Water_Level_Sensor1.VCC, U1.VCC, U1.AVCC, C4.+, R1.Pin_0, S1.leg0, R2.Pin_1
  GND: Capacitive_Soil_Moisture_Sensor1.GND, Q1.E, Water_Level_Sensor1.GND, U1.GND, C4.-, VCC1.-, U2.GND
  N2: D1.C, Mod1.-
  N3: Q1.B, Mod1.+
  N4: Q1.C, U1.D7
  N5: Water_Level_Sensor1.SIG, U1.D12
  N6: Mod1.S, U1.D6_(PWM)
  N7: U1.RESET, R1.Pin_1
  N8: U1.D0_(RX), U2.RXD
  N9: U1.D1_(TX), U2.TXD
  N10: U1.XLAT1, XTAL1.pin_0, C1.1
  N11: U1.XLAT2, C2.2
  N12: C1.2, C2.1
  N13: U2.VCC, U2.CH_PD, R2.Pin_0

custom parts:
  water pump/motor: WATER PUMP BY ARDUBLOCKTR
  DFRobot Capacitive Soil Moisture Sensor V1.0: DFRobot Capacitive Soil Moisture Sensor V1.0 This product measures soil moisture levels by capacitive sensing, rather than resistive sensing like other types of moisture sensor. It is made of a corrosion resistant material giving it a long service life. Insert it into soil and impress your friends with the real-time soil moisture data! The product includes an on-board voltage regulator which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
  Water Level Sensor: A water level sensor. This sensor operates at 3V to 5V. The Sig (signal) pin outputs an analogue signal that is in proportion to the amount of water in contact with the sensor.
  KY-019 5V Relay Module: KY-019 5V Relay module, used to control AC circuits. (Special thanks to vanepp for fixing the PCB holes and other errors)
  ESP8266 WiFi Module: Generic WiFi Module based on the ESP8266 with onboard PCB antenna and UART communications
